# Fritzing sketch Microwave-controller (saved by Fritzing 0.9.3b)

parts:
  WeMos_D1_Mini1 = WeMos D1 Mini
  S4 = Momentary Switch [part_number=STOP package=ksa_sealed_tac_switch]
  S7 = Toggle Switch [part_number=DOOR package=THT]
  U1 = RELAY [part_number="5V RELAY" package=relay-t9a]
  S8 = Momentary Switch [part_number=START package=ksa_sealed_tac_switch]
  U2 = RELAY [part_number="FAN RELAY" package=relay-t9a]
  U3 = RELAY [part_number="MAGNETRON RELAY" package=relay-t9a]
  Компонент1 = 0.56" 7-segment LED Backpack [part_number=DISPLAY]
  Q1 = NPN-Transistor [part_number=2N2222 package="TO92 [THT]"]
  R1 = Resistor [tolerance=±5% resistance=1k package=THT]
  J1 = Piezo Speaker [part_number=PIEZO]

nets:
  5V: WeMos_D1_Mini1.5V, Компонент1.VDD
  N1: WeMos_D1_Mini1.D0, R1.Pin_0
  N2: WeMos_D1_Mini1.D1, U1.COIL1
  N3: WeMos_D1_Mini1.D2, Компонент1.SDA
  N4: WeMos_D1_Mini1.D3, Компонент1.SCL
  N5: WeMos_D1_Mini1.D5, S8.1
  N6: WeMos_D1_Mini1.D6, S4.1
  N7: WeMos_D1_Mini1.D7, S7.COM
  GND: WeMos_D1_Mini1.G, U1.COIL2, U1.NO, S8.3, Компонент1.GND, Q1.E
  N8: S4.3, S7.L2
  N9: U1.MAIN, U2.COIL2, U3.COIL1
  24V: U2.COIL1, U3.COIL2
  N10: Q1.B, R1.Pin_1
  N11: Q1.C, J1.pin2
  9V: J1.pin1

custom parts:
  0.56" 7-segment LED Backpack: This 0.56" 7-segment LED display includes a driver chip for simple control via an I2C interface. The backpack features address-selection jumpers so you can connect up to eight displays on a single I2C bus.
